# Fritzing sketch schematic_car (saved by Fritzing 0.9.3b)
breadboards: 1

parts:
  U1 = JOYSTICK-PSP1000 [package=joystick-psp1000]
  SP1 = SPEAKER [package=pcb_mount_speaker]
  S1 = H-Bridge with L298N
  DI1 = 7-Segment LED Display [package=THT]
  Part3 = Arduino Mega 2560 (Rev3)
  LED1 = smd LED [color="Red (633nm)" package="1206 [SMD]"]
  R1 = Resistor [tolerance=±5% resistance=220 package="2512 [SMD]"]
  DFPlayer_Mini1 = DFPlayer MINI [package="DIP (Dual Inline) [THT]"]
  S2 = H-Bridge with L298N
  e-radionica_com1 = LM393 LDR breakout [part_number=100027]
  LCD = 2.4 Touchscreen TFT Breakout w:MicroSD
  QRE1113_Sensor_Breakout1 = QRE1113 Miniature Reflective Object Sensor Breakout
  QRE1113_Sensor_Breakout2 = QRE1113 Miniature Reflective Object Sensor Breakout
  VCC1 = 4 x AAA Battery Mount
  Arduino_UNO = Arduino Uno (Rev3)
  R2 = Resistor [tolerance=±5% resistance=220 package="2512 [SMD]"]
  M4 = DC Motor
  M5 = DC Motor
  M6 = DC Motor
  M7 = DC Motor
  SG2 = Buzzer 12mm [package=buzzer-12mm-ns]
  IC1 = Voltage Regulator [package=to220-igo]

nets:
  GND: U1.GND, S1.GND, DI1.commAnode#7, Part3.GND, LED1.cathode, DFPlayer_Mini1.GND#6, S2.GND, e-radionica_com1.GND, LCD.GND, QRE1113_Sensor_Breakout1.GND, QRE1113_Sensor_Breakout2.GND, VCC1.-, Arduino_UNO.GND, SG2.1, IC1.GND
  VCC: U1.VCC, S1.5V, DI1.commAnode#2, DFPlayer_Mini1.VCC, S2.5V, e-radionica_com1.VCC, QRE1113_Sensor_Breakout1.VCC, QRE1113_Sensor_Breakout2.VCC, IC1.OUT
  N1: U1.X, Part3.A2
  N2: U1.Y, Part3.A1
  N3: SP1.+, DFPlayer_Mini1.SPK2
  N4: SP1.-, R1.Pin_0
  12V: S1.12V, S2.12V, VCC1.+, IC1.IN
  N5: S1.ENA, Part3.D5_PWM
  N6: S1.IN1, Part3.D30
  N7: S1.IN2, Part3.D31
  N8: S1.IN3, Part3.D32
  N9: S1.IN4, Part3.D33
  N10: S1.ENB, Part3.D6_PWM
  N11: S1.M1-01, M5.pin_2
  N12: S1.M1-02, M5.pin_1
  N13: S1.M2-01, M4.pin_1
  N14: S1.M2-02, M4.pin_2
  N15: S1.ENA-5V, Part3.D4_PWM
  N16: S1.ENB-5V, Part3.D7_PWM
  N17: DI1.cathodeE, Part3.D45
  N18: DI1.cathodeD, Part3.D44
  N19: DI1.cathodeC, Part3.D42
  N20: DI1.cathodeB, Part3.D47
  N21: DI1.cathodeA, Part3.D46
  N22: DI1.cathodeF, Part3.D43
  N23: DI1.cathodeG, Part3.D40
  N24: Part3.A0, e-radionica_com1.AO
  N25: Part3.D21/SCL, Part3.SCL, Arduino_UNO.A5/SCL
  N26: Part3.D20/SDA, Part3.SDA, Arduino_UNO.A4/SDA
  N27: Part3.D14/TX3, SG2.2
  N28: Part3.D12_PWM, LED1.anode
  N29: Part3.D11_PWM, S2.ENB-5V
  N30: Part3.D10_PWM, S2.ENB
  N31: Part3.D9_PWM, S2.ENA-5V
  N32: Part3.D8_PWM, S2.ENA
  5V: Part3.5V, Arduino_UNO.VIN
  N33: Part3.D22, QRE1113_Sensor_Breakout2.OUT
  N34: Part3.D24, QRE1113_Sensor_Breakout1.OUT
  N35: Part3.D34, S2.IN1
  N36: Part3.D35, S2.IN2
  N37: Part3.D36, S2.IN3
  N38: Part3.D37, S2.IN4
  N39: Part3.D50, R2.Pin_1
  N40: Part3.D52, DFPlayer_Mini1.TX
  N41: R1.Pin_1, DFPlayer_Mini1.SPK1
  N42: DFPlayer_Mini1.RX, R2.Pin_0
  N43: S2.M1-01, M7.pin_2
  N44: S2.M1-02, M7.pin_1
  N45: S2.M2-01, M6.pin_1
  N46: S2.M2-02, M6.pin_2
  N47: LCD.CS, Arduino_UNO.D13/SCK
  N48: LCD.C/D, Arduino_UNO.D12/MISO
  N49: LCD.WR, Arduino_UNO.D11_PWM/MOSI
  N50: LCD.RD, Arduino_UNO.D10_PWM/SS
  N51: LCD.RST, Arduino_UNO.D9_PWM
  N52: LCD.LITE, Arduino_UNO.D8
  N53: LCD.X+, Arduino_UNO.D7
  N54: LCD.Y+, Arduino_UNO.D6_PWM
  N55: LCD.X-, Arduino_UNO.D5_PWM
  N56: LCD.Y-, Arduino_UNO.D4
  N57: LCD.D0, Arduino_UNO.D3_PWM
  N58: LCD.D1, Arduino_UNO.D2
  VIN: LCD.VIN, Arduino_UNO.5V
  N59: LCD.IM0, Arduino_UNO.A0
  N60: LCD.IM1, Arduino_UNO.A1
  N61: LCD.IM2, Arduino_UNO.A2
  N62: LCD.IM3, Arduino_UNO.A3
  N63: LCD.SD_CS, Arduino_UNO.3V3

custom parts:
  H-Bridge with L298N: h-bridge
  DFPlayer MINI: MP3 module by DFRobot.com for playing Music from an SD-Card. Supports WAV and MP3 files.
  2.4 Touchscreen TFT Breakout w:MicroSD: Add some jazz & pizzazz to your project with a color touchscreen LCD. This TFT display is 2.4" diagonal with a bright (4 white-LED) backlight and it's colorful! 240x320 pixels with individual RGB pixel control, this has way more resolution than a black and white 128x64 display. As a bonus, this display has a resistive touchscreen attached to it already, so you can detect finger presses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
  QRE1113 Miniature Reflective Object Sensor Breakout: The QRE1113 Miniature Reflective Object Sensor is a product of Fairchild Semiconductor. The breakout board operates at 5V. The optimal sensing distance is 3mm.
